# Fritzing sketch Circuit (saved by Fritzing 0.9.0b)
perfboards: 1

parts:
  PWM1 = PCA9685 16x12-bit PWM Breakout
  S1 = Square Pushbutton
  Q2 = Basic FET N-Channel [package="TO220 [THT]"]
  Q3 = Basic FET N-Channel [package="TO220 [THT]"]
  LED1 = RGB LED (com. anode, rbg) [package="5 mm [THT]"]
  Q1 = Basic FET N-Channel [package="TO220 [THT]"]
  Raspberry_Pi_rev1 = Raspberry Pi B rev2
  Power_plug1 = Power plug
  C1 = Electrolytic Capacitor [capacitance=1µF package="100 mil [THT, electrolytic]"]

nets:
  N1: PWM1.no_name_yet#0, Q1.drain
  N2: PWM1.no_name_yet#1, Q2.drain
  N3: PWM1.no_name_yet#2, Q3.drain
  N4: PWM1.no_name_yet#601, PWM1.no_name_yet#1000, PWM1.no_name_yet#1002
  N5: PWM1.no_name_yet#603, Raspberry_Pi_rev1.GPIO_3
  N6: PWM1.no_name_yet#604, Raspberry_Pi_rev1.GPIO_2
  N7: PWM1.no_name_yet#605, Raspberry_Pi_rev1.3V3
  N8: S1.leg0, Q1.gate, Raspberry_Pi_rev1.GND
  N9: S1.leg1, Raspberry_Pi_rev1.GPIO_17
  N10: Q2.source, LED1.common_anode
  N11: Q3.source, LED1.blue_cathode
  N12: LED1.red_cathode, Q1.source
  N13: LED1.green_cathode, Power_plug1.VCC, C1.+
  N14: Power_plug1.GND, C1.-
