# Fritzing sketch Circuit board design (saved by Fritzing 0.8.3b)
perfboards: 1

parts:
  PWM1 = PCA9685 16x12-bit PWM Breakout
  Raspberry_Pi_rev1 = Raspberry Pi rev2
  Q2 = Basic FET N-Channel [package="TO220 [THT]"]
  Q3 = Basic FET N-Channel [package="TO220 [THT]"]
  LED1 = RGB LED (com. anode, rbg) [package="5 mm [THT]"]
  Q1 = Basic FET N-Channel [package="TO220 [THT]"]
  S1 = Square Pushbutton  # not connected
  VCC1 = 4 x AAA Battery Mount
  S2 = Square Pushbutton
  C1 = Electrolytic Capacitor [capacitance=1000μF package="1010 [SMD, electrolytic]"]  # not connected

nets:
  N1: PWM1.no_name_yet#0, Q1.gate
  N2: PWM1.no_name_yet#1, Q2.gate
  N3: PWM1.no_name_yet#2, Q3.gate
  N4: PWM1.no_name_yet#601, PWM1.no_name_yet#1000, S2.leg1
  N5: PWM1.no_name_yet#603, Raspberry_Pi_rev1.GIPO_3, Raspberry_Pi_rev1.GND, Raspberry_Pi_rev1.GPIO_24
  N6: PWM1.no_name_yet#604, Raspberry_Pi_rev1.GIPO_2, Raspberry_Pi_rev1.GPIO_23
  N7: PWM1.no_name_yet#605, Raspberry_Pi_rev1.3V3
  N8: Raspberry_Pi_rev1.GPIO_17, Raspberry_Pi_rev1.GPIO_22
  N9: Q2.drain, LED1.green_cathode
  N10: Q3.drain, LED1.blue_cathode
  N11: LED1.red_cathode, Q1.drain
  N12: LED1.common_anode, VCC1.+
