# Fritzing sketch Circuit (saved by Fritzing 0.8.3b)
perfboards: 1

parts:
  PWM1 = PCA9685 16x12-bit PWM Breakout
  Raspberry_Pi_rev1 = Raspberry Pi rev2
  S1 = Square Pushbutton
  Q2 = Basic FET N-Channel [package="TO220 [THT]"]
  Q3 = Basic FET N-Channel [package="TO220 [THT]"]
  LED1 = RGB LED (com. anode, rbg) [package="5 mm [THT]"]
  Q1 = Basic FET N-Channel [package="TO220 [THT]"]

nets:
  N1: PWM1.no_name_yet#0, Q1.drain
  N2: PWM1.no_name_yet#1, Q2.drain
  N3: PWM1.no_name_yet#2, Q3.drain
  N4: PWM1.no_name_yet#601, PWM1.no_name_yet#1000, PWM1.no_name_yet#1002, Raspberry_Pi_rev1.GND, S1.leg0
  N5: Raspberry_Pi_rev1.GPIO_17, S1.leg1
  N6: Q2.source, LED1.common_anode
  N7: Q3.source, LED1.blue_cathode
  N8: LED1.red_cathode, Q1.source
